// Logisim project ALU.circ as structural Verilog: 2 circuits, main circuit main
// ALU
module main (
  input  [31:0] ALU_SOURCE_X,
  input  [31:0] ALU_SOURCE_Y,
  input  [3:0] ALU_OPERATION,
  output LT,
  output EQ,
  output GT,
  output [31:0] ALU_RESULT,
  output ADD_OVERFLOW,
  output SUB_OVERFLOW,
  output DIV_BY_ZERO
);

  wire and_1_out, and_2_out, and_5_out, and_6_out, IS_ADD, IS_DIV, IS_SUB, not_1_out, not_2_out, not_3_out,
       not_5_out, not_6_out, not_7_out, or_1_out, or_2_out, X_NEG_MSB, Y_ZERO;

  not not_1 (not_1_out, ALU_SOURCE_X[31]);
  not not_2 (not_2_out, ALU_SOURCE_Y[31]);
  not not_3 (not_3_out, ALU_RESULT[31]);
  and and_1 (and_1_out, not_1_out, not_2_out, ALU_RESULT[31]);
  and and_2 (and_2_out, ALU_SOURCE_X[31], ALU_SOURCE_Y[31], not_3_out);
  and and_3 (DIV_BY_ZERO, IS_DIV, Y_ZERO);
  ALUResult aluresult_1 (
    .ALU_SOURCE_X(ALU_SOURCE_X), .ALU_SOURCE_Y(ALU_SOURCE_Y), .ALU_OPERATION(ALU_OPERATION),
    .ALU_RESULT(ALU_RESULT));
  Comparator #(.width(32), .mode("unsigned")) comparator_1 (
    .a(ALU_SOURCE_Y), .b({32{1'b0}}), .eq(Y_ZERO));  // open: gt, lt
  Comparator #(.width(4), .mode("unsigned")) comparator_2 (
    .a(ALU_OPERATION), .b(4'b1000), .gt(IS_ADD));  // open: eq, lt
  or or_1 (or_1_out, and_1_out, and_2_out);
  and and_4 (ADD_OVERFLOW, or_1_out, IS_ADD);
  not not_4 (X_NEG_MSB, ALU_SOURCE_X[31]);
  Comparator #(.width(4), .mode("unsigned")) comparator_3 (
    .a(ALU_OPERATION), .b(4'b1000), .eq(IS_SUB));  // open: gt, lt
  not not_5 (not_5_out, X_NEG_MSB);
  not not_6 (not_6_out, ALU_SOURCE_Y[31]);
  Comparator #(.width(32)) comparator_4 (.a(ALU_SOURCE_X), .b(ALU_SOURCE_Y), .gt(GT), .eq(EQ), .lt(LT));
  and and_5 (and_5_out, not_5_out, not_6_out, ALU_RESULT[31]);
  and and_6 (and_6_out, X_NEG_MSB, ALU_SOURCE_Y[31], not_7_out);
  not not_7 (not_7_out, ALU_RESULT[31]);
  Comparator #(.width(4), .mode("unsigned")) comparator_5 (
    .a(ALU_OPERATION), .b(4'b0111), .eq(IS_DIV));  // open: gt, lt
  or or_2 (or_2_out, and_5_out, and_6_out);
  and and_7 (SUB_OVERFLOW, or_2_out, IS_SUB);

  // Other names for the same wires on the sheet: ADD_OVER = ADD_OVERFLOW; DIV_ZERO = DIV_BY_ZERO;
  //   OP[3:0] = ALU_OPERATION; RESULT[31:0] = ALU_RESULT; RES_MSB = ALU_RESULT[31]; SUB_OVER = SUB_OVERFLOW;
  //   X[31:0] = ALU_SOURCE_X; X_MSB = ALU_SOURCE_X[31]; Y[31:0] = ALU_SOURCE_Y; Y_MSB = ALU_SOURCE_Y[31]

  // Notes on the sheet:
  //   ALU MODULE
endmodule

module ALUResult (
  input  [31:0] ALU_SOURCE_X,
  input  [31:0] ALU_SOURCE_Y,
  input  [3:0] ALU_OPERATION,
  output [31:0] ALU_RESULT
);

  wire comparator_1_lt, comparator_2_lt, comparator_3_lt, comparator_4_lt;
  wire [4:0] ALU_Y_5;
  wire [31:0] _0, _1, _2, _3, _4, _6, _7, _8, _9, divider_1_out, multiplexer_1_out, multiplexer_2_out,
       multiplexer_3_out, negator_1_out, negator_2_out, negator_3_out, negator_4_out;

  Bit_Extender #(.in_width(32), .out_width(5)) bit_extender_1 (.in(ALU_SOURCE_Y), .out(ALU_Y_5));
  Negator #(.width(32)) negator_1 (.in(ALU_SOURCE_X), .out(negator_1_out));
  Comparator #(.width(32)) comparator_1 (.a(ALU_SOURCE_X), .b({32{1'b0}}), .lt(comparator_1_lt));  // open: gt, eq
  Negator #(.width(32)) negator_2 (.in(ALU_SOURCE_Y), .out(negator_2_out));
  Comparator #(.width(32)) comparator_2 (.a(ALU_SOURCE_Y), .b({32{1'b0}}), .lt(comparator_2_lt));  // open: gt, eq
  Multiplexer #(.width(32)) multiplexer_1 (
    .in0(ALU_SOURCE_X), .in1(negator_1_out), .out(multiplexer_1_out), .sel(comparator_1_lt));  // open: en
  Multiplexer #(.width(32)) multiplexer_2 (
    .in0(ALU_SOURCE_Y), .in1(negator_2_out), .out(multiplexer_2_out), .sel(comparator_2_lt));  // open: en
  Shifter #(.width(32)) shifter_1 (.in(ALU_SOURCE_X), .\dist (ALU_Y_5), .out(_0));
  assign _2 = ALU_SOURCE_X & ALU_SOURCE_Y;  // AND_Gate and_1, 32 bits wide
  assign _4 = ALU_SOURCE_X ^ ALU_SOURCE_Y;  // XOR_Gate xor_1, 32 bits wide
  Multiplier #(.width(32)) multiplier_1 (.a(ALU_SOURCE_X), .b(ALU_SOURCE_Y), .out(_6));  // open: cin, cout
  Subtractor #(.width(32)) subtractor_1 (.a(ALU_SOURCE_Y), .b(ALU_SOURCE_X), .out(_8));  // open: bin, bout
  Divider #(.width(32)) divider_1 (
    .a(multiplexer_1_out), .b(multiplexer_2_out), .out(divider_1_out));  // open: upper, rem
  Negator #(.width(32)) negator_3 (.in(divider_1_out), .out(negator_3_out));
  Comparator #(.width(32)) comparator_3 (.a(ALU_SOURCE_X), .b({32{1'b0}}), .lt(comparator_3_lt));  // open: gt, eq
  Shifter #(.width(32), .shift("lr")) shifter_2 (.in(ALU_SOURCE_X), .\dist (ALU_Y_5), .out(_1));
  assign _3 = ALU_SOURCE_X | ALU_SOURCE_Y;  // OR_Gate or_1, 32 bits wide
  Adder #(.width(32)) adder_1 (.a(ALU_SOURCE_X), .b(ALU_SOURCE_Y), .out(_9));  // open: cin, cout
  Multiplexer #(.width(32)) multiplexer_3 (
    .in0(divider_1_out), .in1(negator_3_out), .out(multiplexer_3_out), .sel(comparator_3_lt));  // open: en
  Negator #(.width(32)) negator_4 (.in(multiplexer_3_out), .out(negator_4_out));
  Multiplexer #(.width(32)) multiplexer_4 (
    .in0(multiplexer_3_out), .in1(negator_4_out), .out(_7), .sel(comparator_4_lt));  // open: en
  Comparator #(.width(32)) comparator_4 (.a(ALU_SOURCE_Y), .b({32{1'b0}}), .lt(comparator_4_lt));  // open: gt, eq
  Multiplexer #(.select(4), .width(32)) multiplexer_5 (
    .in0(_0), .in1(_1), .in2(_2), .in3(_3), .in4(_4), .in5({ALU_SOURCE_Y[31:16], ALU_SOURCE_X[15:0]}),
    .in6(_6), .in7(_7), .in8(_8), .in9(_9), .in10(_9), .in11(_9), .in12(_9), .in13(_9), .in14(_9), .in15(_9),
    .out(ALU_RESULT), .sel(ALU_OPERATION));  // open: en

  // Other names for the same wires on the sheet: _5[31:0] = {ALU_SOURCE_Y[31:16], ALU_SOURCE_X[15:0]};
  //   ALU_X[31:0] = ALU_SOURCE_X; ALU_Y[31:0] = ALU_SOURCE_Y; ALU_OP[3:0] = ALU_OPERATION
endmodule
