// Logisim project CMP.circ as structural Verilog: 1 circuit, main circuit main
// CMP
module main (
  input  LT,
  input  EQ,
  input  GT,
  input  [2:0] CQ_QUERY,
  input  CR_WRITE,
  input  CLOCK,
  output [2:0] CR_VAL,
  output CQ_PASSED
);

  wire and_1_out, and_2_out, and_3_out, HAVE_WRITTEN, not_1_out, not_2_out, or_1_out, or_3_out, or_4_out;
  wire [2:0] multiplexer_1_out;

  or or_1 (or_1_out, CR_WRITE, not_1_out);
  Register #(.width(1)) register_1 (.D(CR_WRITE), .en(or_1_out), .Q(HAVE_WRITTEN), .clk(CLOCK));  // open: clr
  not not_1 (not_1_out, HAVE_WRITTEN);
  and and_1 (and_1_out, CQ_QUERY[0], CR_VAL[0]);
  and and_2 (and_2_out, CQ_QUERY[1], CR_VAL[1]);
  and and_3 (and_3_out, CQ_QUERY[2], CR_VAL[2]);
  or or_2 (CQ_PASSED, and_1_out, and_2_out, and_3_out);
  Multiplexer #(.width(3)) multiplexer_1 (
    .in0(3'b111), .in1({LT, EQ, GT}), .out(multiplexer_1_out), .sel(or_3_out));  // open: en
  or or_3 (or_3_out, HAVE_WRITTEN, CR_WRITE);
  not not_2 (not_2_out, HAVE_WRITTEN);
  or or_4 (or_4_out, not_2_out, CR_WRITE);
  Register #(.width(3)) register_2 (.D(multiplexer_1_out), .en(or_4_out), .Q(CR_VAL), .clk(CLOCK));  // open: clr

  // Other names for the same wires on the sheet: CLK = CLOCK; GT_BIT = CQ_QUERY[0]; EQ_BIT = CQ_QUERY[1];
  //   LT_BIT = CQ_QUERY[2]; PASSED = CQ_PASSED; VAL[2:0] = CR_VAL; VAL_GT = CR_VAL[0]; VAL_EQ = CR_VAL[1];
  //   VAL_LT = CR_VAL[2]; WRITE = CR_WRITE

  // Notes on the sheet:
  //   CR MODULE
endmodule
