// Logisim project CPU.circ as structural Verilog: 1 circuit, main circuit main
// CPU
module main (
  input  [31:0] INSTRUCTION,
  input  [23:0] CURRENT_PC,
  input  CQ_PASSED,
  input  [31:0] REG_1_VAL,
  input  [31:0] REG_2_VAL,
  input  [31:0] REG_3_VAL,
  input  [31:0] ALU_RESULT,
  input  [31:0] MEM_OUT,
  output [23:0] JUMP_ADDRESS,
  output [2:0] CQ_QUERY,
  output CR_WRITE,
  output [3:0] REG_1_READ,
  output [3:0] REG_2_READ,
  output [3:0] REG_3_WRITE,
  output [31:0] REG_WRITE_VAL,
  output REG_WRITE,
  output [31:0] ALU_SOURCE_X,
  output [31:0] ALU_SOURCE_Y,
  output [3:0] ALU_OPERATION,
  output [23:0] MEM_ADDR,
  output [31:0] MEM_IN,
  output MEM_WRITE
);

  wire comparator_1_eq, comparator_3_eq, comparator_4_eq, comparator_5_eq, comparator_8_lt, or_1_out;
  wire [1:1] comparator_6_eq;
  wire [23:0] adder_1_out, multiplexer_2_out;
  wire [31:0] bit_extender_1_out, bit_extender_2_out, bit_extender_3_out, bit_extender_4_out,
       multiplexer_1_out, multiplexer_4_out;

  assign bit_extender_1_out = {{16{INSTRUCTION[15]}}, INSTRUCTION[15:0]};  // Bit_Extender bit_extender_1
  assign bit_extender_2_out = {{12{INSTRUCTION[19]}}, INSTRUCTION[19:0]};  // Bit_Extender bit_extender_2
  assign bit_extender_3_out = {{8{INSTRUCTION[23]}}, INSTRUCTION[23:0]};  // Bit_Extender bit_extender_3
  Comparator #(.width(4), .mode("unsigned")) comparator_1 (
    .a(INSTRUCTION[31:28]), .b(4'b1111), .eq(comparator_1_eq));  // open: gt, lt
  Comparator #(.width(4), .mode("unsigned")) comparator_2 (
    .a(INSTRUCTION[31:28]), .b(4'b1011), .eq(MEM_WRITE));  // open: gt, lt
  Adder #(.width(24)) adder_1 (.a(CURRENT_PC), .b(24'h1), .out(adder_1_out));  // open: cin, cout
  Comparator #(.width(4), .mode("unsigned")) comparator_3 (
    .a(INSTRUCTION[31:28]), .b(4'b1011), .eq(comparator_3_eq));  // open: gt, lt
  Comparator #(.width(4), .mode("unsigned")) comparator_4 (
    .a(INSTRUCTION[31:28]), .b(4'b1101), .eq(comparator_4_eq));  // open: gt, lt
  Comparator #(.width(4), .mode("unsigned")) comparator_5 (
    .a(INSTRUCTION[31:28]), .b(4'b1111), .eq(comparator_5_eq));  // open: gt, lt
  Multiplexer #(.width(32), .enable("false")) multiplexer_1 (
    .in0(bit_extender_2_out), .in1(bit_extender_3_out), .out(multiplexer_1_out), .sel(comparator_1_eq));
  Adder #(.width(24)) adder_2 (.a(REG_1_VAL[23:0]), .b(multiplexer_2_out), .out(MEM_ADDR));  // open: cin, cout
  Multiplexer #(.width(24), .enable("false")) multiplexer_2 (
    .in0(REG_2_VAL[23:0]), .in1(bit_extender_1_out[23:0]), .out(multiplexer_2_out), .sel(INSTRUCTION[24]));
  Comparator #(.width(4), .mode("unsigned")) comparator_6 (
    .a(INSTRUCTION[31:28]), .b(4'b1111), .eq(comparator_6_eq[1]));  // open: gt, lt
  Comparator #(.width(4), .mode("unsigned")) comparator_7 (
    .a(INSTRUCTION[31:28]), .b(4'b1101), .eq(CR_WRITE));  // open: gt, lt
  or or_1 (or_1_out, comparator_3_eq, comparator_4_eq, comparator_5_eq);
  not not_1 (REG_WRITE, or_1_out);
  assign bit_extender_4_out = {{16{INSTRUCTION[15]}}, INSTRUCTION[15:0]};  // Bit_Extender bit_extender_4
  Comparator #(.width(4), .mode("unsigned")) comparator_8 (
    .a(INSTRUCTION[31:28]), .b(4'b1100), .lt(comparator_8_lt));  // open: gt, eq
  Multiplexer #(.select(2), .width(24), .enable("false")) multiplexer_3 (
    .in0(adder_1_out), .in1(adder_1_out), .in2(REG_2_VAL[23:0]), .in3(INSTRUCTION[23:0]), .out(JUMP_ADDRESS),
    .sel({comparator_6_eq[1], INSTRUCTION[24]}));
  Multiplexer #(.width(32), .enable("false")) multiplexer_4 (
    .in0(multiplexer_1_out), .in1(bit_extender_4_out), .out(multiplexer_4_out), .sel(comparator_8_lt));
  Multiplexer #(.width(32), .enable("false")) multiplexer_5 (
    .in0(REG_2_VAL), .in1(multiplexer_4_out), .out(ALU_SOURCE_Y), .sel(INSTRUCTION[24]));
  Multiplexer #(.select(4), .width(32), .enable("false")) multiplexer_6 (
    .in0(ALU_RESULT), .in1(ALU_RESULT), .in2(ALU_RESULT), .in3(ALU_RESULT), .in4(ALU_RESULT),
    .in5(ALU_RESULT), .in6(ALU_RESULT), .in7(ALU_RESULT), .in8(ALU_RESULT), .in9(ALU_RESULT), .in10(MEM_OUT),
    .in11(REG_3_VAL), .in12(ALU_RESULT), .in13(REG_3_VAL), .in14(ALU_RESULT), .in15(REG_3_VAL),
    .out(REG_WRITE_VAL), .sel(INSTRUCTION[31:28]));

  assign ALU_OPERATION = INSTRUCTION[31:28];
  assign ALU_SOURCE_X = REG_1_VAL;
  assign CQ_QUERY = INSTRUCTION[27:25];
  assign MEM_IN = REG_3_VAL;
  assign REG_1_READ = INSTRUCTION[19:16];
  assign REG_2_READ = INSTRUCTION[3:0];
  assign REG_3_WRITE = INSTRUCTION[23:20];

  // Other names for the same wires on the sheet: IMM = INSTRUCTION[24]; INST[31:0] = INSTRUCTION;
  //   ALU_SRC_X[31:0] = REG_1_VAL; ALU_SRC_Y[31:0] = ALU_SOURCE_Y; CUR_PC[23:0] = CURRENT_PC;
  //   IMM16[15:0] = INSTRUCTION[15:0]; IMM20[19:0] = INSTRUCTION[19:0]; IMM24[23:0] = INSTRUCTION[23:0];
  //   RI[3:0] = INSTRUCTION[3:0]; RS[3:0] = INSTRUCTION[19:16]; RD[3:0] = INSTRUCTION[23:20];
  //   CQ[2:0] = INSTRUCTION[27:25]; ALU_OP[3:0] = INSTRUCTION[31:28]; OPCODE[3:0] = INSTRUCTION[31:28];
  //   JUMP_ADDR[23:0] = JUMP_ADDRESS

  // Notes on the sheet:
  //   the address to jump to
  //   reg to read from/write to
  //   the value to write to register
  //   the comparison we are making
  //   whether we should write to cr reg
  //   reg to read from
  //   reg to read from
  //   if we should write to register
  //   1st arg of operation (reg1)
  //   2nd arg of operation (reg2)
  //   the next operation to compute
  //   address of mem_out
  //   the data to overwrite mem_out with
  //   if we should write to mem
  //   INSTRUCTION MODULE
  //   CR MODULE
  //   REGISTER FILE MODULE
  //   ALU MODULE
  //   MEMORY MODULE
  //   the current instruction being executed A
  //   current value of reg 1
  //   current value of reg 2
  //   current value of reg 3
  //   the arithmetic result
  //   the contents at mem_addr
  //   the program counter of the inst being executed A
  //   whether or not the comparison passed
endmodule
