// Logisim project NPC.circ as structural Verilog: 1 circuit, main circuit main
// NPC
module main (
  input  CQ_PASSED,
  input  [31:0] INSTRUCTION,
  input  [23:0] CURRENT_PC,
  input  [23:0] JUMP_ADDRESS,
  output [23:0] NEXT_PC
);

  wire and_1_out, comparator_1_eq;
  wire [23:0] adder_1_out;

  Adder #(.width(24)) adder_1 (.a(CURRENT_PC), .b(24'h1), .out(adder_1_out));  // open: cin, cout
  Comparator #(.width(4), .mode("unsigned")) comparator_1 (
    .a(INSTRUCTION[31:28]), .b(4'b1111), .eq(comparator_1_eq));  // open: gt, lt
  Multiplexer #(.width(24), .enable("false")) multiplexer_1 (
    .in0(adder_1_out), .in1(JUMP_ADDRESS), .out(NEXT_PC), .sel(and_1_out));
  and and_1 (and_1_out, comparator_1_eq, CQ_PASSED);

  // Other names for the same wires on the sheet: CUR_PC[23:0] = CURRENT_PC; INST[31:0] = INSTRUCTION;
  //   JUMP[23:0] = JUMP_ADDRESS; NEXT[23:0] = NEXT_PC

  // Notes on the sheet:
  //   NPC MODULE
endmodule
