// Logisim project PIP.circ as structural Verilog: 1 circuit, main circuit main
// PIP
module main (
  input  CQ_PASSED,
  input  [31:0] INSTRUCTION_IN,
  input  [23:0] PC_IN,
  input  CLOCK,
  output [31:0] INSTRUCTION_OUT,
  output [23:0] PC_OUT
);

  wire and_1_out, comparator_1_eq;
  wire [31:0] multiplexer_1_out;

  Multiplexer #(.width(32)) multiplexer_1 (
    .in0(INSTRUCTION_IN), .in1({32{1'b0}}), .out(multiplexer_1_out), .sel(and_1_out));  // open: en
  and and_1 (and_1_out, CQ_PASSED, comparator_1_eq);
  Register #(.width(32)) register_1 (.D(multiplexer_1_out), .Q(INSTRUCTION_OUT), .clk(CLOCK));  // open: en, clr
  Comparator #(.width(4), .mode("unsigned")) comparator_1 (
    .a(INSTRUCTION_OUT[31:28]), .b(4'b1111), .eq(comparator_1_eq));  // open: gt, lt

  assign PC_OUT = PC_IN;

  // Other names for the same wires on the sheet: CLK = CLOCK

  // Notes on the sheet:
  //   PIPELINE MODULE
endmodule
