// Logisim project REG.circ as structural Verilog: 1 circuit, main circuit main
// REG
module main (
  input  CLOCK,
  input  [3:0] REG_1_READ,
  input  [3:0] REG_2_READ,
  input  [3:0] REG_3_WRITE,
  input  [31:0] REG_WRITE_VAL,
  input  REG_WRITE,
  output [31:0] R00,
  output [31:0] R01,
  output [31:0] R02,
  output [31:0] R03,
  output [31:0] R04,
  output [31:0] R05,
  output [31:0] R06,
  output [31:0] R07,
  output [31:0] REG_1_VAL,
  output [31:0] REG_2_VAL,
  output [31:0] REG_3_VAL,
  output [31:0] R08,
  output [31:0] R09,
  output [31:0] R10,
  output [31:0] R11,
  output [31:0] R12,
  output [31:0] R13,
  output [31:0] R14,
  output [31:0] R15
);

  wire and_1_out, and_2_out, and_3_out, and_4_out, and_5_out, and_6_out, and_7_out, and_8_out, and_9_out,
       and_10_out, and_11_out, and_12_out, and_13_out, and_14_out, and_15_out, and_16_out;
  wire [15:0] which_reg;
  wire [31:0] _0, _1, _2, _3, _4, _5, _6, _7, _8, _9, _10, _11, _12, _13, _14, _15;

  Decoder #(.select(4), .enable("false")) decoder_1 (
    .out0(which_reg[0]), .out1(which_reg[1]), .out2(which_reg[2]), .out3(which_reg[3]), .out4(which_reg[4]),
    .out5(which_reg[5]), .out6(which_reg[6]), .out7(which_reg[7]), .out8(which_reg[8]), .out9(which_reg[9]),
    .out10(which_reg[10]), .out11(which_reg[11]), .out12(which_reg[12]), .out13(which_reg[13]),
    .out14(which_reg[14]), .out15(which_reg[15]), .sel(REG_3_WRITE));
  and and_1 (and_1_out, which_reg[0], REG_WRITE);
  and and_2 (and_2_out, which_reg[1], REG_WRITE);
  and and_3 (and_3_out, which_reg[2], REG_WRITE);
  and and_4 (and_4_out, which_reg[3], REG_WRITE);
  and and_5 (and_5_out, which_reg[4], REG_WRITE);
  and and_6 (and_6_out, which_reg[5], REG_WRITE);
  and and_7 (and_7_out, which_reg[6], REG_WRITE);
  and and_8 (and_8_out, which_reg[7], REG_WRITE);
  and and_9 (and_9_out, which_reg[8], REG_WRITE);
  and and_10 (and_10_out, which_reg[9], REG_WRITE);
  and and_11 (and_11_out, which_reg[10], REG_WRITE);
  and and_12 (and_12_out, which_reg[11], REG_WRITE);
  and and_13 (and_13_out, which_reg[12], REG_WRITE);
  Register #(.width(32)) register_1 (.D(_0), .en(and_1_out), .Q(R00), .clk(CLOCK));  // open: clr
  Register #(.width(32)) register_2 (.D(_1), .en(and_2_out), .Q(R01), .clk(CLOCK));  // open: clr
  Register #(.width(32)) register_3 (.D(_2), .en(and_3_out), .Q(R02), .clk(CLOCK));  // open: clr
  Register #(.width(32)) register_4 (.D(_3), .en(and_4_out), .Q(R03), .clk(CLOCK));  // open: clr
  Register #(.width(32)) register_5 (.D(_4), .en(and_5_out), .Q(R04), .clk(CLOCK));  // open: clr
  Register #(.width(32)) register_6 (.D(_5), .en(and_6_out), .Q(R05), .clk(CLOCK));  // open: clr
  Register #(.width(32)) register_7 (.D(_6), .en(and_7_out), .Q(R06), .clk(CLOCK));  // open: clr
  Register #(.width(32)) register_8 (.D(_7), .en(and_8_out), .Q(R07), .clk(CLOCK));  // open: clr
  Register #(.width(32)) register_9 (.D(_8), .en(and_9_out), .Q(R08), .clk(CLOCK));  // open: clr
  Register #(.width(32)) register_10 (.D(_9), .en(and_10_out), .Q(R09), .clk(CLOCK));  // open: clr
  Register #(.width(32)) register_11 (.D(_10), .en(and_11_out), .Q(R10), .clk(CLOCK));  // open: clr
  Register #(.width(32)) register_12 (.D(_11), .en(and_12_out), .Q(R11), .clk(CLOCK));  // open: clr
  Register #(.width(32)) register_13 (.D(_12), .en(and_13_out), .Q(R12), .clk(CLOCK));  // open: clr
  and and_14 (and_14_out, which_reg[13], REG_WRITE);
  and and_15 (and_15_out, which_reg[14], REG_WRITE);
  and and_16 (and_16_out, which_reg[15], REG_WRITE);
  Multiplexer #(.select(4), .width(32), .enable("false")) multiplexer_1 (
    .in0(R00), .in1(R01), .in2(R02), .in3(R03), .in4(R04), .in5(R05), .in6(R06), .in7(R07), .in8(R08),
    .in9(R09), .in10(R10), .in11(R11), .in12(R12), .in13(R13), .in14(R14), .in15(R15), .out(REG_2_VAL),
    .sel(REG_2_READ));
  Register #(.width(32)) register_14 (.D(_13), .en(and_14_out), .Q(R13), .clk(CLOCK));  // open: clr
  Register #(.width(32)) register_15 (.D(_14), .en(and_15_out), .Q(R14), .clk(CLOCK));  // open: clr
  Register #(.width(32)) register_16 (.D(_15), .en(and_16_out), .Q(R15), .clk(CLOCK));  // open: clr
  Demultiplexer #(.select(4), .width(32), .enable("false")) demultiplexer_1 (
    .out0(_0), .out1(_1), .out2(_2), .out3(_3), .out4(_4), .out5(_5), .out6(_6), .out7(_7), .out8(_8),
    .out9(_9), .out10(_10), .out11(_11), .out12(_12), .out13(_13), .out14(_14), .out15(_15),
    .in(REG_WRITE_VAL), .sel(REG_3_WRITE));
  Multiplexer #(.select(4), .width(32), .enable("false")) multiplexer_2 (
    .in0(R00), .in1(R01), .in2(R02), .in3(R03), .in4(R04), .in5(R05), .in6(R06), .in7(R07), .in8(R08),
    .in9(R09), .in10(R10), .in11(R11), .in12(R12), .in13(R13), .in14(R14), .in15(R15), .out(REG_1_VAL),
    .sel(REG_1_READ));
  Multiplexer #(.select(4), .width(32), .enable("false")) multiplexer_3 (
    .in0(R00), .in1(R01), .in2(R02), .in3(R03), .in4(R04), .in5(R05), .in6(R06), .in7(R07), .in8(R08),
    .in9(R09), .in10(R10), .in11(R11), .in12(R12), .in13(R13), .in14(R14), .in15(R15), .out(REG_3_VAL),
    .sel(REG_3_WRITE));

  // Other names for the same wires on the sheet: _1R[3:0] = REG_1_READ; _1V[31:0] = REG_1_VAL; _2R[3:0] = REG_2_READ;
  //   _2V[31:0] = REG_2_VAL; _3V[31:0] = REG_3_VAL; _3W[3:0] = REG_3_WRITE; clk = CLOCK; RW = REG_WRITE;
  //   RWV[31:0] = REG_WRITE_VAL

  // Notes on the sheet:
  //   REGISTER FILE MODULE
endmodule
